# Fritzing sketch range_finder (saved by Fritzing 0.9.6b)
breadboards: 1

parts:
  Pico_H1 = Raspberry Pi Pico H
  S1 = 0.91 inch OLED I2C Display 128 x 32 Pixels
  HC-SR04_Sensor_1 = HC-SR04 Ultrasonic Distance Sensor

nets:
  VCC: Pico_H1.VBUS, S1.VCC, HC-SR04_Sensor_1.VCC
  GND: Pico_H1.GND, S1.GND, HC-SR04_Sensor_1.GND
  N1: Pico_H1.GP5, S1.SCL
  N2: Pico_H1.GP4, S1.SDA
  N3: Pico_H1.GP3, HC-SR04_Sensor_1.ECHO
  N4: Pico_H1.GP2, HC-SR04_Sensor_1.TRIG

custom parts:
  Raspberry Pi Pico H: Raspberry Pi Pico H. Based around the RP2040 microcontroller the Pico H is a low cost microcontroller device bringing Raspberry Pi quality, cost, and easy of use to the microcontroller space.
